# Fritzing sketch ultimate_machine (saved by Fritzing 0.7.11b)
breadboards: 1

parts:
  Part1 = Arduino Pro Mini 3.3V
  VCC1 = 4 x AAA Battery Mount
  R1 = 10k Ω Resistor [package=THT]
  J1 = Basic Servo
  S3 = Pushbutton [package=THT]

nets:
  N1: Part1.DTR, Part1.TXO
  N2: VCC1.-, J1.gnd, S3.leg0
  N3: VCC1.+, R1.Pin_1, J1.vcc
  N4: R1.Pin_0, S3.leg1
